# Fritzing sketch demo (saved by Fritzing 0.9.3b)
breadboards: 1

parts:
  Arduino_UNO = Arduino Uno (Rev3)
  rotary_sensor = Slide Potentiometer [maximum_resistance=10kΩ]
  Accerometer = Triple Axis Accelerometer Breakout - ADXL335
  Motor = DC Motor
  Motor_Driver = DIP - 10 pins [chip_label=DRV8830 package="DIP (Dual Inline) [THT]"]
  Vcc = 4 x AAA Battery Mount
  R1 = Resistor [tolerance=±5% resistance=10k package=THT]
  R2 = Resistor [tolerance=±5% resistance=10k package=THT]
  R7E-SV4 = mystery part, 5 pins [chip_label=?]
  C1 = Ceramic Capacitor [capacitance=1nF package="1206 [SMD, multilayer]"]

nets:
  N1: Arduino_UNO.A0, rotary_sensor.wiper, R7E-SV4.pin1
  N2: Arduino_UNO.A4/SDA, Motor_Driver.SDA, R2.Pin_1
  GND: Arduino_UNO.GND, rotary_sensor.leg1, Accerometer.GND, Motor_Driver.GND, Vcc.-, R7E-SV4.pin5
  N3: Arduino_UNO.A5/SCL, Motor_Driver.SCL, R1.Pin_1
  to Accelerometer: Arduino_UNO.VIN, rotary_sensor.leg2, Vcc.+, R1.Pin_0, R2.Pin_0
  N4: Accerometer.ZOUT, R7E-SV4.pin4
  N5: Accerometer.YOUT, R7E-SV4.pin3
  N6: Accerometer.XOUT, R7E-SV4.pin2
  5V/from 5V power: Accerometer.VCC, Motor_Driver.VCC
  N7: Motor.pin_1, Motor_Driver.OUT2, C1.1
  N8: Motor.pin_2, Motor_Driver.OUT1, C1.0

custom parts:
  DIP - 10 pins: A DIP stand-in part for whatever IC you want. With 10 pins on a 300mil dual inline package (DIP) footprint.
